// Logisim project LomannLecoq Groupe2.circ as structural Verilog
module Add1 (
  input  A,
  input  B,
  input  C_int,
  output S,
  output G,
  output P
);

  wire xor_1_out;

  xor xor_1 (xor_1_out, A, B);
  and and_1 (G, B, A);
  or or_1 (P, G, xor_1_out);
  xor xor_2 (S, C_int, xor_1_out);
endmodule

module propa (
  input  Cin0,
  input  P0,
  input  G0,
  output Cout0
);

  wire and_1_out;

  and and_1 (and_1_out, P0, Cin0);
  or or_1 (Cout0, G0, and_1_out);
endmodule

module anticipation (
  input  C0,
  input  P0,
  input  G0,
  input  P1,
  input  G1,
  input  P2,
  input  G2,
  input  P3,
  input  G3,
  output C1,
  output C2,
  output C3,
  output C4
);

  wire and_1_out, and_2_out, and_3_out, and_4_out, and_5_out, and_6_out, and_7_out, and_8_out, and_9_out,
       and_10_out;

  and and_1 (and_1_out, C0, P0);
  and and_2 (and_2_out, C0, P0, P1);
  and and_3 (and_3_out, G0, P1);
  and and_4 (and_4_out, C0, P0, P1, P2);
  and and_5 (and_5_out, G0, P1, P2);
  and and_6 (and_6_out, G1, P2);
  and and_7 (and_7_out, C0, P0, P1, P2, P3);
  and and_8 (and_8_out, G0, P1, P2, P3);
  and and_9 (and_9_out, G1, P2, P3);
  and and_10 (and_10_out, G2, P3);
  or or_1 (C1, and_1_out, G0);
  or or_2 (C2, and_2_out, and_3_out, G1);
  or or_3 (C3, and_4_out, and_5_out, and_6_out, G2);
  or or_4 (C4, and_7_out, and_8_out, and_9_out, and_10_out, G3);
endmodule

module UAL (
  input  [15:0] A,
  input  [2:0] in_2,
  input  [15:0] B,
  output out_4,
  output out_5,
  output [15:0] out_6
);

  wire [15:0] adder_1_out, and_1_out, not_1_out, or_1_out, shifter_1_out, shifter_2_out, undriven, xor_1_out;

  Adder #(.width(16)) adder_1 (.a(A), .b(B), .out(adder_1_out));  // open: cin, cout
  soustracteur soustracteur_1 (.A(A), .B(B), .Sortie(undriven));  // open: out_4
  assign and_1_out = A & B;  // AND_Gate and_1, 16 bits wide
  assign not_1_out = ~A;  // NOT_Gate not_1, 16 bits wide
  assign or_1_out = A | B;  // OR_Gate or_1, 16 bits wide
  assign xor_1_out = A ^ B;  // XOR_Gate xor_1, 16 bits wide
  Shifter #(.width(16)) shifter_1 (.in(A), .\dist (4'b1111), .out(shifter_1_out));
  Shifter #(.width(16), .shift("ar")) shifter_2 (.in(A), .\dist (4'b1111), .out(shifter_2_out));
  Multiplexer #(.select(3), .width(16), .enable("false")) multiplexer_1 (
    .in0(adder_1_out), .in1(undriven), .in2(not_1_out), .in3(and_1_out), .in4(or_1_out), .in5(xor_1_out),
    .in6(shifter_1_out), .in7(shifter_2_out), .out({out_5, out_6[14:0]}), .sel(in_2));
  nor nor_1 (out_4, out_6[0], out_6[1], out_6[2], out_6[3], out_6[4], out_6[5], out_6[6], out_6[7], out_6[8], out_6[9], out_6[10], out_6[11], out_6[12], out_6[13], out_6[14], out_5);

  assign out_6[15] = out_5;
endmodule

module add4 (
  input  [3:0] A,
  input  Cint,
  input  [3:0] B,
  output [3:0] sortie
);

  wire add1_1_g, add1_1_p, add1_2_g, add1_2_p, add1_3_g, add1_3_p, add1_4_g, add1_4_p, anticipation_1_c1,
       anticipation_1_c2, anticipation_1_c3;

  Add1 add1_1 (.A(A[0]), .B(B[0]), .G(add1_1_g), .C_int(Cint), .P(add1_1_p));  // open: S
  anticipation anticipation_1 (
    .C0(Cint), .P0(add1_1_p), .G0(add1_1_g), .P1(add1_2_p), .G1(add1_2_g), .P2(add1_3_p), .G2(add1_3_g),
    .P3(add1_4_p), .G3(add1_4_g), .C1(anticipation_1_c1), .C2(anticipation_1_c2), .C3(anticipation_1_c3));  // open: C4
  Add1 add1_2 (.A(A[1]), .B(B[1]), .G(add1_2_g), .C_int(anticipation_1_c1), .P(add1_2_p));  // open: S
  Add1 add1_3 (.A(A[2]), .B(B[2]), .G(add1_3_g), .C_int(anticipation_1_c2), .P(add1_3_p));  // open: S
  Add1 add1_4 (.A(A[3]), .B(B[3]), .G(add1_4_g), .C_int(anticipation_1_c3), .P(add1_4_p));  // open: S
endmodule

module soustracteur (
  input  [15:0] A,
  input  [15:0] Sortie,
  input  [15:0] B,
  output out_4
);

  wire [15:0] not_1_out;

  assign not_1_out = ~B;  // NOT_Gate not_1, 16 bits wide
  Adder #(.width(16)) adder_1 (.a(A), .b(not_1_out), .out(Sortie), .cin(1'b1), .cout(out_4));
endmodule
